# Fritzing sketch Pi Unit (saved by Fritzing 1.0.3b)
breadboards: 1

parts:
  MCU1 = Raspberry Pi Zero
  6DOF_IMU_2Click1 = 6DOF IMU 2Click [chip_label="6DOF IMU 2Click" package="DIP (Dual Inline) [THT]"]
  NEO6M_V1 = NEO6M V2 [chip_label="NEO6M V2" package="DIP (Dual Inline) [THT]"]
  MAX1 = MAX30102 [chip_label=MAX30102 package="DIP (Dual Inline) [THT]"]

nets:
  3V3: MCU1.pin_1, 6DOF_IMU_2Click1.3V3, NEO6M_V1.VCC, MAX1.VIN
  N1: MCU1.pin_3, 6DOF_IMU_2Click1.SDA, MAX1.SDA
  N2: MCU1.pin_5, 6DOF_IMU_2Click1.SCL, MAX1.SCL
  GND: MCU1.pin_6, MCU1.pin_9, 6DOF_IMU_2Click1.GND, NEO6M_V1.GND, MAX1.GND
  N3: MCU1.pin_8, NEO6M_V1.RX
  N4: MCU1.pin_10, NEO6M_V1.TX

custom parts:
  6DOF IMU 2Click: A DIP stand-in part for whatever IC you want. With 8 pins on a 300mil dual inline package (DIP) footprint.
  NEO6M V2: A DIP stand-in part for whatever IC you want. With 8 pins on a 300mil dual inline package (DIP) footprint.
  MAX30102: A DIP stand-in part for whatever IC you want. With 8 pins on a 300mil dual inline package (DIP) footprint.
